// Logisim project masina_de_spalat_finalizata.circ as structural Verilog
module main (
  input  [2:0] Input_bus_1,
  input  Input_3,
  input  [1:0] Input_bus_2,
  input  Input_1,
  input  Input_4,
  input  Input_2,
  input  Input_5,
  input  Input_6,
  input  Input_7,
  input  Input_8,
  input  Input_9,
  output [3:0] Output_bus_1
);

  wire activinactiv_1_iesire, and_gate_1_y, counter_timp_automat1_1_iesire, frecventa_rest_1_iesire,
       numarator_1minut_1_deschidere_usa, selectmode_1_o1, selectmode_1_o2;
  wire [1:0] divizor_frecventa_1_selectie;
  wire [3:0] dcdafisor_1_mii, dcdafisor_1_sute, dcdafisor_1_unit, dcdafisor_1_zeci, muxcifra_1_out_mux;
  wire [6:0] dcd_hexa_7seg_afisor_1_output;
  wire [7:0] mux_temp_1_output;
  wire [11:0] counter_timp_automat1_1_output, mux_moduri_automate_1_iesire,
       spalare_clatire_centrifugare_1_output;

  dcdafisor dcdafisor_1 (
    .\input (counter_timp_automat1_1_output), .unit(dcdafisor_1_unit), .zeci(dcdafisor_1_zeci),
    .sute(dcdafisor_1_sute), .mii(dcdafisor_1_mii));
  divizor_frecventa divizor_frecventa_1 (.clk(Input_8), .reset(Input_7), .selectie(divizor_frecventa_1_selectie));
  mux_temp mux_temp_1 (.enable(selectmode_1_o2), .sel(Input_bus_2), .\output (mux_temp_1_output));
  counter_timp_automat1 counter_timp_automat1_1 (
    .clock(frecventa_rest_1_iesire), .reset(Input_5), .enable(selectmode_1_o2), .enable2(selectmode_1_o1),
    .\input (spalare_clatire_centrifugare_1_output), .input2(mux_moduri_automate_1_iesire),
    .\output (counter_timp_automat1_1_output), .iesire(counter_timp_automat1_1_iesire));
  frecventa_rest frecventa_rest_1 (.CLOCK_IN(Input_8), .reset(Input_9), .iesire(frecventa_rest_1_iesire));
  selectMODE selectmode_1 (.Intrare(and_gate_1_y), .o1(selectmode_1_o1), .o2(selectmode_1_o2));
  LED LED_3 (.in(selectmode_1_o2));
  muxcifra muxcifra_1 (
    .mii_s(dcdafisor_1_unit), .sute_s(dcdafisor_1_zeci), .zeci_s(dcdafisor_1_sute),
    .unitati_s(dcdafisor_1_mii), .sel(divizor_frecventa_1_selectie), .out_mux(muxcifra_1_out_mux));
  mux_anod mux_anod_1 (.sel(divizor_frecventa_1_selectie), .out_anod(Output_bus_1));
  spalare_clatire_centrifugare spalare_clatire_centrifugare_1 (
    .\input (mux_temp_1_output), .clatire_suplimentara(Input_3), .prespalare_suplimentara(Input_4),
    .\output (spalare_clatire_centrifugare_1_output));
  LED LED_2 (.in(selectmode_1_o1));
  numarator_1minut numarator_1minut_1 (
    .clock(frecventa_rest_1_iesire), .reset(Input_6), .enable(counter_timp_automat1_1_iesire),
    .deschidere_usa(numarator_1minut_1_deschidere_usa));
  dcd_hexa_7seg_afisor dcd_hexa_7seg_afisor_1 (.\input (muxcifra_1_out_mux), .\output (dcd_hexa_7seg_afisor_1_output));
  mux_moduri_automate mux_moduri_automate_1 (
    .enable(selectmode_1_o1), .sel(Input_bus_1), .iesire(mux_moduri_automate_1_iesire));
  LED LED_1 (.in(numarator_1minut_1_deschidere_usa));
  _7_Segment_Display L_7_Segment_Display_1 (
    .g(dcd_hexa_7seg_afisor_1_output[0]), .f(dcd_hexa_7seg_afisor_1_output[1]),
    .a(dcd_hexa_7seg_afisor_1_output[6]), .b(dcd_hexa_7seg_afisor_1_output[5]),
    .e(dcd_hexa_7seg_afisor_1_output[2]), .d(dcd_hexa_7seg_afisor_1_output[3]),
    .c(dcd_hexa_7seg_afisor_1_output[4]), .dp(1'b0));
  activINACTIV activinactiv_1 (.A(Input_1), .IESIRE(activinactiv_1_iesire));
  LED LED_4 (.in(activinactiv_1_iesire));
  and_gate and_gate_1 (.A(activinactiv_1_iesire), .B(Input_2), .y(and_gate_1_y));
endmodule

// VHDL entity ddddddddddddd, as the project stores it:
--------------------------------------------------------------------------------
-- Project :
-- File    :
-- Autor   :
-- Date    :
--
--------------------------------------------------------------------------------
-- Description :
--
--------------------------------------------------------------------------------

LIBRARY ieee;
USE ieee.std_logic_1164.all;

ENTITY ddddddddddddd IS
  PORT (
 enable: in std_logic;
 input: in std_logic;
 o: out std_logic
    );
END ddddddddddddd;

--------------------------------------------------------------------------------
--Complete your VHDL description below
--------------------------------------------------------------------------------

ARCHITECTURE TypeArchitecture OF ddddddddddddd IS

BEGIN
process(enable,input)
begin
if enable='1' then
	if input = '1' then o <= '1';
	elsif input = '0' then o <= '0';
	end if;
end if;

end process;

END TypeArchitecture;

// VHDL entity selectMODE, as the project stores it:
--------------------------------------------------------------------------------
-- Project :
-- File    :
-- Autor   :
-- Date    :
--
--------------------------------------------------------------------------------
-- Description :
--
--------------------------------------------------------------------------------

LIBRARY ieee;
USE ieee.std_logic_1164.all;

ENTITY selectMODE IS
  PORT (
  Intrare: in std_logic;
  o1: out std_logic;
  o2: out std_logic
    );
END selectMODE;

--------------------------------------------------------------------------------
--Complete your VHDL description below
--------------------------------------------------------------------------------

ARCHITECTURE TypeArchitecture OF selectMODE IS

BEGIN
process(Intrare)
begin
if Intrare = '1' then o1 <= '1'; o2<= '0';
elsif Intrare = '0' then  o2 <= '1'; o1 <= '0';
end if;
end process;

END TypeArchitecture;

// VHDL entity mux_temp, as the project stores it:
--------------------------------------------------------------------------------
-- Project :
-- File    :
-- Autor   :
-- Date    :
--
--------------------------------------------------------------------------------
-- Description :
--
--------------------------------------------------------------------------------

LIBRARY ieee;
USE ieee.std_logic_1164.all;

USE ieee.std_logic_unsigned.all;

ENTITY mux_temp IS
  PORT (
  enable : in std_logic;
  sel: in std_logic_vector ( 1 downto 0);
  output: out std_logic_vector(7 downto 0)
    );
END mux_temp;

--------------------------------------------------------------------------------
--Complete your VHDL description below
--------------------------------------------------------------------------------

ARCHITECTURE TypeArchitecture OF mux_temp IS

BEGIN

process(enable,sel)
begin
if enable ='1' then
case sel is
when "00" => output<="00011110"; -- 30 grade -> 30 secunde
when "01" => output<="00110010"; -- 40 -> 50 secunde
when "10" => output<="01000110"; -- 60 -> 70 secunde
when others => output<="10010110"; -- 90 -> 150 secunde
end case;
end if;
end process;

END TypeArchitecture;

// VHDL entity spalare_clatire_centrifugare, as the project stores it:
--------------------------------------------------------------------------------
-- Project :
-- File    :
-- Autor   :
-- Date    :
--
--------------------------------------------------------------------------------
-- Description :
--
--------------------------------------------------------------------------------

LIBRARY ieee;
USE ieee.std_logic_unsigned.all;
USE ieee.std_logic_1164.all;
use ieee.std_logic_arith.all;

ENTITY spalare_clatire_centrifugare IS
  PORT (
  input: in std_logic_vector (7 downto 0);
  clatire_suplimentara : in std_logic;
  prespalare_suplimentara: in std_logic;
  output: out std_logic_vector (11 downto 0)
  
    );
END spalare_clatire_centrifugare;

--------------------------------------------------------------------------------
--Complete your VHDL description below
--------------------------------------------------------------------------------

ARCHITECTURE TypeArchitecture OF spalare_clatire_centrifugare IS

BEGIN

process(input,clatire_suplimentara,prespalare_suplimentara)
variable auxiliar : std_logic_vector(11 downto 0);
begin
auxiliar := "0000" & input;
auxiliar := auxiliar + "100101100000"; -- 40 de minute in sec
if (clatire_suplimentara ='1') then
   auxiliar := auxiliar+"001001011000";
end if;
if (prespalare_suplimentara ='1') then
  auxiliar := auxiliar+"001001011000";
   end if;
  output <= auxiliar;
   end process;

END TypeArchitecture;

// VHDL entity mux_moduri_automate, as the project stores it:
--------------------------------------------------------------------------------
-- Project :
-- File    :
-- Autor   :
-- Date    :
--
--------------------------------------------------------------------------------
-- Description :
--
--------------------------------------------------------------------------------

LIBRARY ieee;
USE ieee.std_logic_1164.all;

USE ieee.std_logic_unsigned.all;

ENTITY mux_moduri_automate IS
  PORT (
 enable:in std_logic;
 sel:in std_logic_vector (2 downto 0);
 iesire: out std_logic_vector (11 downto 0)
    );
END mux_moduri_automate;

--------------------------------------------------------------------------------
--Complete your VHDL description below
--------------------------------------------------------------------------------

ARCHITECTURE TypeArchitecture OF mux_moduri_automate IS

BEGIN

process(enable,sel)
begin
if (enable='1') then
   case sel is 
   when "000" => iesire <="100101101111"; -- 30 de grade, spalare rapida
   when "001" => iesire <="100110001101"; -- 60 de grade, camasi
   when "010" => iesire <="101111010001"; -- 40 de grade, culori inchise
   when "011" => iesire <="101111010001"; -- 40 de grade, rufe murdare
   when "100" => iesire <="110000000011"; -- 90 de grade, antialergic
   when others =>iesire <="000000000000";
  end case ;
end if;
end process;

END TypeArchitecture;

// VHDL entity counter_timp_automat1, as the project stores it:
--------------------------------------------------------------------------------
-- Project :
-- File    :
-- Autor   :
-- Date    :
--
--------------------------------------------------------------------------------
-- Description :
--
--------------------------------------------------------------------------------

LIBRARY ieee;
USE ieee.std_logic_1164.all;
USE ieee.std_logic_unsigned.all;
use ieee.std_logic_arith.all;


ENTITY counter_timp_automat1 IS
  PORT (
  clock:in std_logic;
  reset,enable,enable2: in std_logic;
  input: in std_logic_vector (11 downto 0);
  input2: in std_logic_vector (11 downto 0);
  output: out std_logic_vector (11 downto 0);
  iesire: out std_logic
    );
END counter_timp_automat1;

--------------------------------------------------------------------------------
--Complete your VHDL description below
--------------------------------------------------------------------------------

ARCHITECTURE TypeArchitecture OF counter_timp_automat1 IS

BEGIN

process(clock,reset,enable,enable2)
variable auxiliar : std_logic_vector(11 downto 0):=input;
variable auxiliar2 : std_logic_vector(11 downto 0):=input2;
begin

if enable='1' then
if (auxiliar /= 0) then
    if(reset ='1') then
    auxiliar := input;
    elsif (clock'event and clock='1')
    then auxiliar:=auxiliar - 1;
    end if;
end if;
output<=auxiliar;
if auxiliar = "000000000000" then iesire <='1';
end if;
end if;


if enable2='1' then
if (auxiliar2 /= 0) then
    if(reset ='1') then
    auxiliar2 := input2;
    elsif (clock'event and clock='1')
    then auxiliar2:=auxiliar2 - 1;
    end if;
end if;
output<=auxiliar2;
if auxiliar2 = "000000000000" then iesire <='1';
end if;
end if;
end process;

END TypeArchitecture;

// VHDL entity frecventa_rest, as the project stores it:
--------------------------------------------------------------------------------
-- Project :
-- File    :
-- Autor   :
-- Date    :
--
--------------------------------------------------------------------------------
-- Description :
--
--------------------------------------------------------------------------------

LIBRARY ieee;
USE ieee.std_logic_1164.all;
USE ieee.std_logic_UNSIGNED.all;

ENTITY frecventa_rest IS
  PORT (
  CLOCK_IN : IN STD_LOGIC;
  reset: in std_logic;
  iesire: OUT STD_LOGIC
    );
END frecventa_rest;

--------------------------------------------------------------------------------
--Complete your VHDL description below
--------------------------------------------------------------------------------

ARCHITECTURE TypeArchitecture OF frecventa_rest IS

SIGNAL TMP: STD_LOGIC :='0';
BEGIN
PROCESS(CLOCK_IN,reset)

variable aux : integer :=0;
BEGIN

if reset='1' then
iesire<='0';
aux:=0;
elsif CLOCK_IN='1' and CLOCK_IN'event then
if aux = 1_000_000 then
TMP<=not TMP;
aux:=0;
else aux:=aux+1;
end if;
end if;

iesire<=TMP;

END PROCESS;



END TypeArchitecture;

// VHDL entity divizor_frecventa, as the project stores it:
--------------------------------------------------------------------------------
-- Project :
-- File    :
-- Autor   :
-- Date    :
--
--------------------------------------------------------------------------------
-- Description :
--
--------------------------------------------------------------------------------

LIBRARY ieee;
USE ieee.std_logic_1164.all;
use ieee.std_logic_unsigned.all;
use ieee.numeric_std.all;
ENTITY divizor_frecventa IS
  PORT (
clk, reset: in std_logic;
        selectie: out std_logic_vector(1 downto 0)
    );
END divizor_frecventa;

--------------------------------------------------------------------------------
--Complete your VHDL description below
--------------------------------------------------------------------------------

ARCHITECTURE TypeArchitecture OF divizor_frecventa IS
signal x: std_logic_vector(15 downto 0):="0000000000000000";
BEGIN
process(clk, reset)
variable auxiliar: integer:=0;
begin
if(reset='1') then x<="0000000000000000";
elsif (clk='1' and clk'event) then 
         auxiliar:=conv_integer(x);
         if(auxiliar=65_535) then x<="0000000000000000";
         else x<=x+"0000000000000001";
         end if;
selectie<=x(14 downto 13);
end if;
end process;


END TypeArchitecture;

// VHDL entity mux_anod, as the project stores it:
--------------------------------------------------------------------------------
-- Project :
-- File    :
-- Autor   :
-- Date    :
--
--------------------------------------------------------------------------------
-- Description :
--
--------------------------------------------------------------------------------

LIBRARY ieee;
USE ieee.std_logic_1164.all;

ENTITY mux_anod IS
  PORT (
  		sel: in std_logic_vector(1 downto 0);
  		out_anod:out std_logic_vector(3 downto 0)
    );
END mux_anod;

--------------------------------------------------------------------------------
--Complete your VHDL description below
--------------------------------------------------------------------------------

ARCHITECTURE TypeArchitecture OF mux_anod IS

BEGIN

		with sel select out_anod<= "0001" when "00",
							  "0010" when "01",
							  "0100" when "10",
							  "1000" when "11",
							  "0000" when others;
END TypeArchitecture;

// VHDL entity muxcifra, as the project stores it:
--------------------------------------------------------------------------------
-- Project :
-- File    :
-- Autor   :
-- Date    :
--
--------------------------------------------------------------------------------
-- Description :
--
--------------------------------------------------------------------------------

LIBRARY ieee;
USE ieee.std_logic_1164.all;

ENTITY muxcifra IS
  PORT (
  		mii_s,sute_s,zeci_s,unitati_s:in std_logic_vector(3 downto 0);
  		sel:in std_logic_vector(1 downto 0);
  		out_mux:out std_logic_vector(3 downto 0)
    );
END muxcifra;

--------------------------------------------------------------------------------
--Complete your VHDL description below
--------------------------------------------------------------------------------

ARCHITECTURE TypeArchitecture OF muxcifra IS

BEGIN

with sel select out_mux<=unitati_s when "00",
					zeci_s when "01",
					sute_s when "10",
					mii_s when others;


END TypeArchitecture;

// VHDL entity dcdafisor, as the project stores it:
--------------------------------------------------------------------------------
-- Project :
-- File    :
-- Autor   :
-- Date    :
--
--------------------------------------------------------------------------------
-- Description :
--
--------------------------------------------------------------------------------


LIBRARY ieee;
USE ieee.std_logic_1164.all;
USE ieee.std_logic_unsigned.all;
use ieee.numeric_std.all;
use ieee.numeric_std.all;

ENTITY dcdafisor IS
	PORT (
		input : in std_logic_vector(11 downto 0);
		unit, zeci, sute, mii : out std_logic_vector(3 downto 0)
    	);
END dcdafisor;

--------------------------------------------------------------------------------
--Complete your VHDL description below
--------------------------------------------------------------------------------

ARCHITECTURE arh OF dcdafisor IS

	signal a : natural;
BEGIN
	a <= conv_integer(input);
	unit <= std_logic_vector(to_unsigned(a rem 10, 4));
	zeci <= std_logic_vector(to_unsigned(a/10 rem 10, 4));
	sute <= std_logic_vector(to_unsigned(a/100 rem 10, 4));
	mii <= std_logic_vector(to_unsigned(a/1000 rem 10, 4));
END arh;

// VHDL entity numarator_1minut, as the project stores it:
--------------------------------------------------------------------------------
-- Project :
-- File    :
-- Autor   :
-- Date    :
--
--------------------------------------------------------------------------------
-- Description :
--
--------------------------------------------------------------------------------

LIBRARY ieee;
USE ieee.std_logic_1164.all;
use ieee.std_logic_unsigned.all;

ENTITY numarator_1minut IS
  PORT (
   clock,reset:in std_logic;
 -- output:out std_logic_vector(5 downto 0);
  enable:in std_logic;
  deschidere_usa : out std_logic
    );
END numarator_1minut;

--------------------------------------------------------------------------------
--Complete your VHDL description below
--------------------------------------------------------------------------------

ARCHITECTURE TypeArchitecture OF numarator_1minut IS

signal aux23: std_logic;
begin

  process(clock, reset,enable)
    variable aux: std_logic_vector(5 downto 0) := "000000";
  begin
  if enable ='1' then
    if reset = '1' then
      aux := "000000";
    elsif (clock'event and clock = '1') then
      if aux = "111100" then
        aux := "111111"; -- Opriți numărătorul
      elsif aux /= "111111" then
        aux := aux + 1; -- Numărătorul continuă să crească
      end if;
    end if;
    if(aux="111100") then
    aux23 <='1';

    end if;
    
    
    
    end if;
  end process;
deschidere_usa <= aux23;

END TypeArchitecture;

// VHDL entity dcd_hexa_7seg_afisor, as the project stores it:
--------------------------------------------------------------------------------
-- Project :
-- File    :
-- Autor   :
-- Date    :
--
--------------------------------------------------------------------------------
-- Description :
--
--------------------------------------------------------------------------------

LIBRARY ieee;
USE ieee.std_logic_1164.all;

ENTITY dcd_hexa_7seg_afisor IS
  	PORT (
  		input : in std_logic_vector(3 downto 0);
  		output : out std_logic_vector(6 downto 0)
    	);
END dcd_hexa_7seg_afisor;

--------------------------------------------------------------------------------
--Complete your VHDL description below
--------------------------------------------------------------------------------

ARCHITECTURE arh OF dcd_hexa_7seg_afisor IS

BEGIN

	output <= 	"1111110" when input = x"0" else
				"0110000" when input = x"1" else
				"1101101" when input = x"2" else
				"1111001" when input = x"3" else
				"0110011" when input = x"4" else
				"1011011" when input = x"5" else
				"1011111" when input = x"6" else
				"1110000" when input = x"7" else
				"1111111" when input = x"8" else
				"1111011" when input = x"9" else
				"1110111" when input = x"A" else
				"0011111" when input = x"B" else
				"1001110" when input = x"C" else
				"0111101" when input = x"D" else
				"1001111" when input = x"E" else
				"1000111" when input = x"F"; 
END arh;

// VHDL entity activINACTIV, as the project stores it:
--------------------------------------------------------------------------------
-- Project :
-- File    :
-- Autor   :
-- Date    :
--
--------------------------------------------------------------------------------
-- Description :
--
--------------------------------------------------------------------------------

LIBRARY ieee;
USE ieee.std_logic_1164.all;
USE ieee.std_logic_unsigned.all;


ENTITY activINACTIV IS
  PORT (
  A: in std_logic;
  IESIRE : OUT STD_LOGIC
    );
END activINACTIV;

--------------------------------------------------------------------------------
--Complete your VHDL description below
--------------------------------------------------------------------------------

ARCHITECTURE TypeArchitecture OF activINACTIV IS

BEGIN

process(A)
begin 

if A = '1' then Iesire <= A;
else Iesire <= '0';
end if;
end process;

END TypeArchitecture;

// VHDL entity and_gate, as the project stores it:
--------------------------------------------------------------------------------
-- Project :
-- File    :
-- Autor   :
-- Date    :
--
--------------------------------------------------------------------------------
-- Description :
--
--------------------------------------------------------------------------------

LIBRARY ieee;
USE ieee.std_logic_1164.all;

ENTITY and_gate IS
  PORT (
  A: in std_logic;
  B:in std_logic;
  y: out std_logic
    );
END and_gate;

--------------------------------------------------------------------------------
--Complete your VHDL description below
--------------------------------------------------------------------------------

ARCHITECTURE TypeArchitecture OF and_gate IS

BEGIN

y<= A and B;

END TypeArchitecture;
